// Logisim project e2449080 (1).circ as structural Verilog: 1 circuit, main circuit main
module main (
  input  O3,
  input  O0,
  input  O1,
  input  O2,
  input  A1,
  input  A0,
  input  B0,
  input  B0_2,
  output G,
  output L,
  output E,
  output L8,
  output S,
  output C,
  output L0,
  output L1,
  output L2,
  output L9,
  output L3,
  output L4,
  output L5,
  output L7,
  output L6
);

  wire and_1_out, and_2_out, and_3_out, and_4_out, and_5_out, and_6_out, and_7_out, and_8_out, and_10_out,
       and_11_out, and_12_out, and_13_out, and_14_out, and_15_out, and_16_out, and_17_out, and_18_out,
       and_19_out, and_20_out, and_21_out, and_22_out, and_23_out, and_24_out, and_25_out, and_26_out,
       and_27_out, and_28_out, and_29_out, and_30_out, and_31_out, and_32_out, and_33_out, and_34_out,
       and_35_out, and_36_out, and_37_out, and_38_out, and_39_out, and_40_out, and_41_out, and_42_out,
       and_43_out, and_44_out, and_45_out, and_46_out, and_47_out, and_48_out, and_49_out, and_50_out,
       and_51_out, and_52_out, and_53_out, and_54_out, and_55_out, and_56_out, and_57_out, and_58_out,
       and_59_out, and_60_out, and_61_out, and_62_out, and_63_out, and_64_out, and_65_out, and_66_out,
       and_67_out, and_68_out, and_69_out, and_70_out, and_71_out, and_72_out, and_73_out, and_74_out,
       and_75_out, and_76_out, and_77_out, and_78_out, and_79_out, and_80_out, and_81_out, and_82_out,
       and_83_out, and_84_out, and_85_out, controlled_buffer_1_out, controlled_buffer_2_out,
       controlled_buffer_3_out, controlled_buffer_4_out, controlled_buffer_5_out, controlled_buffer_6_out,
       controlled_buffer_7_out, controlled_buffer_8_out, controlled_buffer_9_out, controlled_buffer_10_out,
       controlled_buffer_11_out, controlled_buffer_12_out, controlled_buffer_13_out,
       controlled_buffer_14_out, controlled_buffer_15_out, controlled_buffer_16_out,
       controlled_buffer_17_out, controlled_buffer_18_out, controlled_buffer_19_out,
       controlled_buffer_20_out, controlled_buffer_21_out, controlled_buffer_22_out,
       controlled_buffer_23_out, controlled_buffer_24_out, controlled_buffer_25_out,
       controlled_buffer_26_out, controlled_buffer_27_out, controlled_buffer_28_out,
       controlled_buffer_29_out, controlled_buffer_30_out, controlled_buffer_31_out,
       controlled_buffer_32_out, controlled_buffer_33_out, controlled_buffer_34_out,
       controlled_buffer_35_out, controlled_buffer_36_out, n3_to_8_decoder_74138_1_p1,
       n3_to_8_decoder_74138_1_p2, n3_to_8_decoder_74138_1_p3, n3_to_8_decoder_74138_1_p4,
       n3_to_8_decoder_74138_1_p5, n3_to_8_decoder_74138_1_p6, n3_to_8_decoder_74138_1_p7,
       n3_to_8_decoder_74138_1_p8, n3_to_8_decoder_74138_1_p9, n3_to_8_decoder_74138_1_p10,
       n3_to_8_decoder_74138_2_p2, n3_to_8_decoder_74138_2_p4, n3_to_8_decoder_74138_2_p6,
       n3_to_8_decoder_74138_2_p7, n3_to_8_decoder_74138_2_p8, n3_to_8_decoder_74138_2_p9,
       n3_to_8_decoder_74138_2_p10, n3_to_8_decoder_74138_2_p11, not_3_out, not_4_out, not_5_out, not_6_out,
       not_7_out, not_8_out, not_9_out, not_15_out, not_16_out, not_17_out, not_18_out, not_19_out,
       not_20_out, not_21_out, not_22_out, not_23_out, not_24_out, not_25_out, not_26_out, not_27_out,
       not_28_out, not_29_out, not_30_out, not_31_out, not_32_out, not_33_out, not_34_out, not_35_out,
       not_36_out, not_37_out, not_38_out, not_39_out, not_40_out, not_41_out, not_42_out, not_43_out,
       not_44_out, not_45_out, not_46_out, not_47_out, not_48_out, not_49_out, not_50_out, not_51_out,
       not_52_out, not_53_out, not_54_out, not_55_out, not_56_out, not_57_out, not_58_out, not_59_out,
       not_60_out, not_61_out, not_62_out, not_63_out, not_64_out, not_65_out, not_66_out, not_67_out,
       or_2_out, or_3_out, or_4_out, or_5_out, or_6_out, or_8_out, or_9_out, or_10_out, or_12_out, or_13_out,
       or_14_out, or_15_out, or_16_out, or_17_out, or_18_out, or_19_out, or_20_out, or_21_out, or_23_out,
       or_24_out, or_25_out, or_26_out, or_27_out, or_28_out, or_29_out, or_30_out, or_31_out, or_32_out,
       or_34_out, or_35_out, or_37_out, or_39_out, or_41_out, or_42_out, or_43_out, or_44_out, or_45_out;

  // _3_to_8_decoder__74138 #(.Facing("south")) 3_to_8_decoder_74138_1: pin names not known; wires that end beside it: n3_to_8_decoder_74138_1_p1, n3_to_8_decoder_74138_1_p2, n3_to_8_decoder_74138_1_p3, n3_to_8_decoder_74138_1_p4, n3_to_8_decoder_74138_1_p5, n3_to_8_decoder_74138_1_p6, n3_to_8_decoder_74138_1_p7, n3_to_8_decoder_74138_1_p8, n3_to_8_decoder_74138_1_p9, n3_to_8_decoder_74138_1_p10, 1'b1, 1'b0, 1'b0
  not not_1 (L1, n3_to_8_decoder_74138_1_p4);
  not not_2 (L0, n3_to_8_decoder_74138_1_p2);
  // _3_to_8_decoder__74138 #(.Facing("south")) 3_to_8_decoder_74138_2: pin names not known; wires that end beside it: O0, n3_to_8_decoder_74138_2_p2, O1, n3_to_8_decoder_74138_2_p4, O2, n3_to_8_decoder_74138_2_p6, n3_to_8_decoder_74138_2_p7, n3_to_8_decoder_74138_2_p8, n3_to_8_decoder_74138_2_p9, n3_to_8_decoder_74138_2_p10, n3_to_8_decoder_74138_2_p11, 1'b1, 1'b0, 1'b0
  not not_3 (not_3_out, n3_to_8_decoder_74138_2_p10);
  not not_4 (not_4_out, n3_to_8_decoder_74138_2_p6);
  not not_5 (not_5_out, n3_to_8_decoder_74138_2_p7);
  not not_6 (not_6_out, n3_to_8_decoder_74138_2_p9);
  not not_7 (not_7_out, n3_to_8_decoder_74138_2_p8);
  not not_8 (not_8_out, n3_to_8_decoder_74138_2_p4);
  not not_9 (not_9_out, n3_to_8_decoder_74138_2_p2);
  assign controlled_buffer_1_out = not_9_out ? A1 : 1'bz;  // Controlled_Buffer controlled_buffer_1
  not not_10 (L2, n3_to_8_decoder_74138_1_p6);
  not not_11 (L3, n3_to_8_decoder_74138_1_p7);
  not not_12 (L4, n3_to_8_decoder_74138_1_p8);
  not not_13 (L6, n3_to_8_decoder_74138_1_p10);
  not not_14 (L5, n3_to_8_decoder_74138_1_p9);
  not not_15 (not_15_out, n3_to_8_decoder_74138_2_p11);
  assign controlled_buffer_2_out = not_9_out ? A0 : 1'bz;  // Controlled_Buffer controlled_buffer_2
  assign controlled_buffer_3_out = not_9_out ? B0 : 1'bz;  // Controlled_Buffer controlled_buffer_3
  assign controlled_buffer_4_out = not_9_out ? B0_2 : 1'bz;  // Controlled_Buffer controlled_buffer_4
  or or_1 (n3_to_8_decoder_74138_1_p1, or_3_out, and_81_out);
  not not_16 (not_16_out, controlled_buffer_1_out);
  and and_1 (and_1_out, not_16_out, controlled_buffer_2_out);
  and and_2 (and_2_out, controlled_buffer_2_out, not_17_out);
  not not_17 (not_17_out, controlled_buffer_4_out);
  and and_3 (and_3_out, controlled_buffer_1_out, not_18_out);
  not not_18 (not_18_out, controlled_buffer_2_out);
  and and_4 (and_4_out, controlled_buffer_3_out, controlled_buffer_4_out);
  or or_2 (or_2_out, or_5_out, or_6_out);
  or or_3 (or_3_out, or_2_out, or_45_out);
  and and_5 (and_5_out, and_1_out, controlled_buffer_3_out);
  or or_4 (or_4_out, and_5_out, and_2_out);
  and and_6 (and_6_out, and_3_out, and_4_out);
  or or_5 (or_5_out, or_8_out, or_9_out);
  or or_6 (or_6_out, or_29_out, or_10_out);
  or or_7 (n3_to_8_decoder_74138_1_p5, or_15_out, 1'b0);
  or or_8 (or_8_out, or_4_out, and_10_out);
  assign controlled_buffer_5_out = not_8_out ? A1 : 1'bz;  // Controlled_Buffer controlled_buffer_5
  and and_7 (and_7_out, controlled_buffer_5_out, controlled_buffer_6_out);
  or or_9 (or_9_out, or_20_out, or_23_out);
  or or_10 (or_10_out, or_43_out, or_44_out);
  or or_11 (n3_to_8_decoder_74138_1_p3, or_12_out, and_80_out);
  assign controlled_buffer_6_out = not_8_out ? A0 : 1'bz;  // Controlled_Buffer controlled_buffer_6
  assign controlled_buffer_7_out = not_8_out ? B0 : 1'bz;  // Controlled_Buffer controlled_buffer_7
  assign controlled_buffer_8_out = not_8_out ? B0_2 : 1'bz;  // Controlled_Buffer controlled_buffer_8
  and and_8 (and_8_out, controlled_buffer_8_out, controlled_buffer_7_out);
  and and_9 (L9, and_7_out, and_8_out);
  or or_12 (or_12_out, and_6_out, or_14_out);
  and and_10 (and_10_out, controlled_buffer_6_out, controlled_buffer_8_out);
  and and_11 (and_11_out, controlled_buffer_6_out, controlled_buffer_7_out);
  and and_12 (and_12_out, controlled_buffer_8_out, controlled_buffer_5_out);
  and and_13 (and_13_out, controlled_buffer_7_out, controlled_buffer_5_out);
  or or_13 (or_13_out, or_17_out, or_18_out);
  or or_14 (or_14_out, or_13_out, or_42_out);
  or or_15 (or_15_out, and_13_out, C);
  or or_16 (or_16_out, and_11_out, and_12_out);
  or or_17 (or_17_out, or_16_out, and_17_out);
  or or_18 (or_18_out, or_28_out, or_34_out);
  assign controlled_buffer_9_out = not_4_out ? A1 : 1'bz;  // Controlled_Buffer controlled_buffer_9
  assign controlled_buffer_10_out = not_4_out ? A0 : 1'bz;  // Controlled_Buffer controlled_buffer_10
  assign controlled_buffer_11_out = not_4_out ? B0 : 1'bz;  // Controlled_Buffer controlled_buffer_11
  assign controlled_buffer_12_out = not_4_out ? B0_2 : 1'bz;  // Controlled_Buffer controlled_buffer_12
  not not_19 (not_19_out, controlled_buffer_11_out);
  not not_20 (not_20_out, controlled_buffer_12_out);
  not not_21 (not_21_out, controlled_buffer_11_out);
  and and_14 (and_14_out, controlled_buffer_10_out, not_19_out);
  or or_19 (or_19_out, and_14_out, and_15_out);
  and and_15 (and_15_out, controlled_buffer_9_out, not_20_out);
  and and_16 (and_16_out, controlled_buffer_9_out, controlled_buffer_10_out);
  and and_17 (and_17_out, controlled_buffer_9_out, not_21_out);
  or or_20 (or_20_out, or_19_out, and_16_out);
  assign controlled_buffer_13_out = not_5_out ? A1 : 1'bz;  // Controlled_Buffer controlled_buffer_13
  assign controlled_buffer_14_out = not_5_out ? A0 : 1'bz;  // Controlled_Buffer controlled_buffer_14
  assign controlled_buffer_15_out = not_5_out ? B0 : 1'bz;  // Controlled_Buffer controlled_buffer_15
  assign controlled_buffer_16_out = not_5_out ? B0_2 : 1'bz;  // Controlled_Buffer controlled_buffer_16
  not not_22 (not_22_out, controlled_buffer_14_out);
  and and_18 (and_18_out, not_22_out, controlled_buffer_16_out);
  and and_19 (and_19_out, controlled_buffer_14_out, not_23_out);
  not not_23 (not_23_out, controlled_buffer_16_out);
  not not_24 (not_24_out, controlled_buffer_13_out);
  and and_20 (and_20_out, not_24_out, not_25_out);
  and and_21 (and_21_out, and_20_out, and_22_out);
  not not_25 (not_25_out, controlled_buffer_15_out);
  and and_22 (and_22_out, controlled_buffer_14_out, controlled_buffer_16_out);
  and and_23 (and_23_out, controlled_buffer_13_out, controlled_buffer_14_out);
  and and_24 (and_24_out, and_23_out, and_25_out);
  and and_25 (and_25_out, controlled_buffer_15_out, controlled_buffer_16_out);
  not not_26 (not_26_out, controlled_buffer_13_out);
  and and_26 (and_26_out, not_26_out, not_27_out);
  not not_27 (not_27_out, controlled_buffer_14_out);
  and and_27 (and_27_out, and_26_out, controlled_buffer_15_out);
  not not_28 (not_28_out, controlled_buffer_16_out);
  and and_28 (and_28_out, not_28_out, not_29_out);
  not not_29 (not_29_out, controlled_buffer_13_out);
  and and_29 (and_29_out, and_28_out, controlled_buffer_15_out);
  not not_30 (not_30_out, controlled_buffer_14_out);
  and and_30 (and_30_out, not_30_out, not_31_out);
  not not_31 (not_31_out, controlled_buffer_15_out);
  and and_31 (and_31_out, and_30_out, controlled_buffer_13_out);
  not not_32 (not_32_out, controlled_buffer_16_out);
  and and_32 (and_32_out, not_32_out, not_33_out);
  not not_33 (not_33_out, controlled_buffer_15_out);
  and and_33 (and_33_out, and_32_out, controlled_buffer_13_out);
  and and_34 (and_34_out, controlled_buffer_14_out, controlled_buffer_15_out);
  and and_35 (and_35_out, and_34_out, controlled_buffer_15_out);
  and and_36 (and_36_out, controlled_buffer_13_out, controlled_buffer_14_out);
  and and_37 (and_37_out, and_36_out, controlled_buffer_16_out);
  or or_21 (or_21_out, and_37_out, and_35_out);
  and and_38 (and_38_out, controlled_buffer_13_out, controlled_buffer_15_out);
  or or_22 (C, and_38_out, or_21_out);
  or or_23 (or_23_out, and_18_out, and_19_out);
  or or_24 (or_24_out, and_21_out, and_24_out);
  or or_25 (or_25_out, and_27_out, and_29_out);
  or or_26 (or_26_out, and_31_out, and_33_out);
  or or_27 (or_27_out, or_24_out, or_25_out);
  or or_28 (or_28_out, or_27_out, or_26_out);
  assign controlled_buffer_17_out = not_7_out ? A1 : 1'bz;  // Controlled_Buffer controlled_buffer_17
  assign controlled_buffer_18_out = not_7_out ? A0 : 1'bz;  // Controlled_Buffer controlled_buffer_18
  assign controlled_buffer_19_out = not_7_out ? B0 : 1'bz;  // Controlled_Buffer controlled_buffer_19
  assign controlled_buffer_20_out = not_7_out ? B0_2 : 1'bz;  // Controlled_Buffer controlled_buffer_20
  not not_34 (not_34_out, controlled_buffer_18_out);
  and and_39 (and_39_out, not_34_out, controlled_buffer_20_out);
  and and_40 (and_40_out, controlled_buffer_18_out, not_35_out);
  not not_35 (not_35_out, controlled_buffer_20_out);
  not not_36 (not_36_out, controlled_buffer_17_out);
  and and_41 (and_41_out, not_36_out, not_37_out);
  and and_42 (and_42_out, and_41_out, controlled_buffer_19_out);
  not not_37 (not_37_out, controlled_buffer_18_out);
  not not_38 (not_38_out, controlled_buffer_19_out);
  and and_43 (and_43_out, controlled_buffer_17_out, and_44_out);
  and and_44 (and_44_out, not_38_out, not_39_out);
  not not_39 (not_39_out, controlled_buffer_20_out);
  not not_40 (not_40_out, controlled_buffer_17_out);
  and and_45 (and_45_out, not_40_out, controlled_buffer_19_out);
  and and_46 (and_46_out, and_45_out, controlled_buffer_20_out);
  and and_47 (and_47_out, controlled_buffer_17_out, and_48_out);
  and and_48 (and_48_out, controlled_buffer_18_out, not_41_out);
  not not_41 (not_41_out, controlled_buffer_19_out);
  not not_42 (not_42_out, controlled_buffer_17_out);
  and and_49 (and_49_out, not_42_out, not_43_out);
  and and_50 (and_50_out, and_49_out, controlled_buffer_20_out);
  not not_43 (not_43_out, controlled_buffer_18_out);
  not not_44 (not_44_out, controlled_buffer_18_out);
  and and_51 (and_51_out, not_44_out, controlled_buffer_19_out);
  and and_52 (and_52_out, and_51_out, controlled_buffer_20_out);
  not not_45 (not_45_out, controlled_buffer_17_out);
  and and_53 (and_53_out, not_45_out, controlled_buffer_19_out);
  or or_29 (or_29_out, and_39_out, and_40_out);
  or or_30 (or_30_out, and_42_out, and_43_out);
  or or_31 (or_31_out, and_46_out, and_47_out);
  or or_32 (or_32_out, and_53_out, and_52_out);
  or or_33 (S, or_32_out, and_50_out);
  or or_34 (or_34_out, or_30_out, or_31_out);
  assign controlled_buffer_21_out = not_6_out ? A1 : 1'bz;  // Controlled_Buffer controlled_buffer_21
  assign controlled_buffer_22_out = not_6_out ? A0 : 1'bz;  // Controlled_Buffer controlled_buffer_22
  assign controlled_buffer_23_out = not_6_out ? B0 : 1'bz;  // Controlled_Buffer controlled_buffer_23
  assign controlled_buffer_24_out = not_6_out ? B0_2 : 1'bz;  // Controlled_Buffer controlled_buffer_24
  not not_46 (not_46_out, controlled_buffer_23_out);
  not not_47 (not_47_out, controlled_buffer_21_out);
  not not_48 (not_48_out, controlled_buffer_23_out);
  not not_49 (not_49_out, controlled_buffer_24_out);
  not not_50 (not_50_out, controlled_buffer_24_out);
  and and_54 (and_54_out, controlled_buffer_22_out, controlled_buffer_23_out);
  not not_51 (not_51_out, controlled_buffer_21_out);
  not not_52 (not_52_out, controlled_buffer_21_out);
  not not_53 (not_53_out, controlled_buffer_22_out);
  not not_54 (not_54_out, controlled_buffer_23_out);
  not not_55 (not_55_out, controlled_buffer_22_out);
  and and_55 (and_55_out, controlled_buffer_23_out, controlled_buffer_24_out);
  not not_56 (not_56_out, controlled_buffer_24_out);
  not not_57 (not_57_out, controlled_buffer_23_out);
  not not_58 (not_58_out, controlled_buffer_22_out);
  not not_59 (not_59_out, controlled_buffer_21_out);
  not not_60 (not_60_out, controlled_buffer_21_out);
  not not_61 (not_61_out, controlled_buffer_23_out);
  and and_56 (and_56_out, controlled_buffer_22_out, controlled_buffer_24_out);
  and and_57 (and_57_out, controlled_buffer_21_out, controlled_buffer_22_out);
  and and_58 (and_58_out, controlled_buffer_23_out, controlled_buffer_24_out);
  not not_62 (not_62_out, controlled_buffer_24_out);
  not not_63 (not_63_out, controlled_buffer_22_out);
  and and_59 (and_59_out, controlled_buffer_23_out, controlled_buffer_21_out);
  and and_60 (and_60_out, controlled_buffer_21_out, not_46_out);
  and and_61 (and_61_out, not_47_out, not_48_out);
  and and_62 (and_62_out, and_61_out, and_63_out);
  and and_63 (and_63_out, not_49_out, controlled_buffer_22_out);
  and and_64 (and_64_out, controlled_buffer_21_out, not_50_out);
  and and_65 (and_65_out, and_64_out, and_54_out);
  and and_66 (and_66_out, not_51_out, controlled_buffer_23_out);
  and and_67 (and_67_out, not_52_out, not_53_out);
  and and_68 (and_68_out, and_67_out, and_69_out);
  and and_69 (and_69_out, not_54_out, controlled_buffer_24_out);
  and and_70 (and_70_out, controlled_buffer_21_out, not_55_out);
  and and_71 (and_71_out, and_70_out, and_55_out);
  and and_72 (and_72_out, not_56_out, not_57_out);
  and and_73 (and_73_out, and_72_out, and_74_out);
  and and_74 (and_74_out, not_58_out, not_59_out);
  and and_75 (and_75_out, not_60_out, not_61_out);
  and and_76 (and_76_out, and_75_out, and_56_out);
  and and_77 (and_77_out, and_57_out, and_58_out);
  and and_78 (and_78_out, not_62_out, not_63_out);
  and and_79 (and_79_out, and_78_out, and_59_out);
  or or_35 (or_35_out, and_60_out, and_62_out);
  or or_36 (G, or_35_out, and_65_out);
  or or_37 (or_37_out, and_66_out, and_68_out);
  or or_38 (L, or_37_out, and_71_out);
  or or_39 (or_39_out, and_73_out, and_76_out);
  or or_40 (E, or_39_out, or_41_out);
  or or_41 (or_41_out, and_77_out, and_79_out);
  assign controlled_buffer_25_out = not_3_out ? A1 : 1'bz;  // Controlled_Buffer controlled_buffer_25
  assign controlled_buffer_26_out = not_3_out ? A0 : 1'bz;  // Controlled_Buffer controlled_buffer_26
  and and_80 (and_80_out, controlled_buffer_25_out, controlled_buffer_27_out);
  assign controlled_buffer_27_out = not_3_out ? B0 : 1'bz;  // Controlled_Buffer controlled_buffer_27
  assign controlled_buffer_28_out = not_3_out ? B0_2 : 1'bz;  // Controlled_Buffer controlled_buffer_28
  and and_81 (and_81_out, controlled_buffer_26_out, controlled_buffer_28_out);
  assign controlled_buffer_29_out = not_15_out ? A1 : 1'bz;  // Controlled_Buffer controlled_buffer_29
  assign controlled_buffer_30_out = not_15_out ? A0 : 1'bz;  // Controlled_Buffer controlled_buffer_30
  assign controlled_buffer_31_out = not_15_out ? B0 : 1'bz;  // Controlled_Buffer controlled_buffer_31
  assign controlled_buffer_32_out = not_15_out ? B0_2 : 1'bz;  // Controlled_Buffer controlled_buffer_32
  not not_64 (not_64_out, controlled_buffer_29_out);
  and and_82 (and_82_out, not_64_out, controlled_buffer_31_out);
  and and_83 (and_83_out, controlled_buffer_29_out, not_65_out);
  not not_65 (not_65_out, controlled_buffer_31_out);
  not not_66 (not_66_out, controlled_buffer_30_out);
  and and_84 (and_84_out, not_66_out, controlled_buffer_32_out);
  and and_85 (and_85_out, controlled_buffer_30_out, not_67_out);
  not not_67 (not_67_out, controlled_buffer_32_out);
  or or_42 (or_42_out, and_82_out, and_83_out);
  or or_43 (or_43_out, and_84_out, and_85_out);
  assign controlled_buffer_33_out = O3 ? A1 : 1'bz;  // Controlled_Buffer controlled_buffer_33
  assign controlled_buffer_34_out = O3 ? A0 : 1'bz;  // Controlled_Buffer controlled_buffer_34
  or or_44 (or_44_out, controlled_buffer_33_out, controlled_buffer_35_out);
  assign controlled_buffer_35_out = O3 ? B0 : 1'bz;  // Controlled_Buffer controlled_buffer_35
  assign controlled_buffer_36_out = O3 ? B0_2 : 1'bz;  // Controlled_Buffer controlled_buffer_36
  or or_45 (or_45_out, controlled_buffer_34_out, controlled_buffer_36_out);

  assign L7 = 1'b0;
  assign L8 = 1'b0;

  // Notes on the sheet:
  //   GREATER
  //   LESS
endmodule
